// Logisim project Zarkhah-610399196-Project.circ as structural Verilog: 29 circuits, main circuit 16bit-incrementer
module main (
  input  [7:0] in_1,
  input  in_2,
  input  [15:0] in_3,
  output [15:0] out_4,
  output [15:0] out_5,
  output [15:0] out_6,
  output [7:0] out_7,
  output [11:0] out_8,
  output [15:0] out_9,
  output out_10,
  output out_11,
  output out_12,
  output [2:0] out_13,
  output [11:0] out_14,
  output [7:0] out_15,
  output out_16,
  output [7:0] out_17,
  output [15:0] out_18,
  output out_19,
  output out_20,
  output [15:0] out_21
);

  wire ac_controller_1_clr, ac_controller_1_inc, ac_controller_1_load, ar_controller_1_clr,
       ar_controller_1_inc, ar_controller_1_load, CLK, clock_1_out, dr_controller_1_inc,
       dr_controller_1_load, e_controller_1_out_7, fgi_controller_1_out_6, fgo_controller_1_out_6,
       ien_controller_1_out_7, ir_controller_1_out_3, ir_controller_1_out_4, ir_controller_1_out_5,
       ir_decoder_1_out_3, memory_controller_1_out_4, n16bit_alu_1_e_2, not_1_out, outr_controller_1_out_5,
       outr_controller_1_out_6, outr_controller_1_out_7, pc_controller_1_clr, pc_controller_1_inc,
       pc_controller_1_load, r_controller_1_out_6, S, s_controller_1_out_5, sc_controller_1_out_5,
       tr_controller_1_out_3, tr_controller_1_out_4, tr_controller_1_out_5;
  wire [7:0] n0_8_1_out_2;
  wire [11:0] n0_12_1_out_2, n0_12_2_out_2;
  wire [15:0] bus_1_out_10, n16bit_alu_1_out_9;

  Clock clock_1 (.out(clock_1_out));
  not not_1 (not_1_out, S);
  and and_1 (CLK, clock_1_out, not_1_out);
  _0_12 u_0_12_1 (.in_1(bus_1_out_10), .out_2(n0_12_1_out_2));
  _0_12 u_0_12_2 (.in_1(bus_1_out_10), .out_2(n0_12_2_out_2));
  _8bit_register INPR (.LD(in_2), .CLR(1'b0), .INR(1'b0), .in_5(in_1), .OUTP(out_17), .CLK(CLK));
  IR_Decoder ir_decoder_1 (.in_1(out_6), .out_2(out_7), .out_3(ir_decoder_1_out_3));
  _0_8 u_0_8_1 (.in_1(bus_1_out_10), .out_2(n0_8_1_out_2));
  S_Controller s_controller_1 (.in_1(out_4), .D(out_7), .in_3(out_6), .I(out_10), .out_5(s_controller_1_out_5));
  D_Flip_Flop #(.trigger("falling")) d_ff_1 (
    .clk(CLK), .D(e_controller_1_out_7), .Q(out_16));  // open: Qn, preset, en, reset
  IEN_Controller ien_controller_1 (
    .in_1(out_4), .D(out_7), .I(out_10), .IR(out_6), .R(out_11), .IEN(out_12), .out_7(ien_controller_1_out_7));
  T_Flip_Flop #(.trigger("falling")) t_ff_1 (
    .clk(CLK), .T(s_controller_1_out_5), .Q(S));  // open: Qn, preset, reset, en
  D_Flip_Flop #(.trigger("falling")) d_ff_2 (
    .clk(CLK), .D(ir_decoder_1_out_3), .Q(out_10));  // open: Qn, preset, en, reset
  OUTR_Controller outr_controller_1 (
    .in_1(out_4), .D(out_7), .in_3(out_6), .I(out_10), .out_5(outr_controller_1_out_5),
    .out_6(outr_controller_1_out_6), .out_7(outr_controller_1_out_7));
  D_Flip_Flop #(.trigger("falling")) d_ff_3 (
    .clk(CLK), .D(ien_controller_1_out_7), .Q(out_12));  // open: Qn, preset, en, reset
  SC_Controller sc_controller_1 (.T(out_4), .D(out_7), .I(out_10), .R(out_11), .out_5(sc_controller_1_out_5));
  _8bit_register OUTR (
    .LD(outr_controller_1_out_5), .CLR(outr_controller_1_out_7), .INR(outr_controller_1_out_6),
    .in_5(n0_8_1_out_2), .OUTP(out_15), .CLK(CLK));
  SC sc_1 (.count_enable(1'b1), .CLK(CLK), .out_4(out_4), .clr(sc_controller_1_out_5));
  _16bit_ALU u_16bit_alu_1 (
    .E(out_16), .T(out_4), .D(out_7), .IR(out_6), .in_7(out_21), .I(out_10), .out_9(n16bit_alu_1_out_9),
    .E_2(n16bit_alu_1_e_2), .INPR(out_17), .in_5(out_18));
  R_Controller r_controller_1 (
    .in_1(out_4), .IEN(out_12), .FGO(out_20), .FGI(out_19), .R(out_11), .out_6(r_controller_1_out_6));
  PC_Controller pc_controller_1 (
    .in_1(out_4), .D(out_7), .in_3(out_21), .in_4(out_18), .IR(out_6), .I(out_10), .R(out_11), .E(out_16),
    .FGO(out_20), .FGI(out_19), .inc(pc_controller_1_inc), .load(pc_controller_1_load),
    .clr(pc_controller_1_clr));
  E_Controller e_controller_1 (
    .in_1(out_4), .D(out_7), .IR(out_6), .I(out_10), .E(out_16), .ALU(n16bit_alu_1_e_2),
    .out_7(e_controller_1_out_7));
  D_Flip_Flop #(.trigger("falling")) d_ff_4 (
    .clk(CLK), .D(r_controller_1_out_6), .Q(out_11));  // open: Qn, preset, en, reset
  AR_Controller ar_controller_1 (
    .in_1(out_4), .D(out_7), .I(out_10), .R(out_11), .load(ar_controller_1_load), .inc(ar_controller_1_inc),
    .clr(ar_controller_1_clr));
  AC_Controller ac_controller_1 (
    .in_1(out_4), .D(out_7), .in_3(out_6), .I(out_10), .load(ac_controller_1_load),
    .inc(ac_controller_1_inc), .clr(ac_controller_1_clr));
  FGI_Controller fgi_controller_1 (
    .in_1(out_4), .I(out_7), .in_3(out_10), .IR(out_6), .in_5(out_19), .out_6(fgi_controller_1_out_6));
  Memory_Controller memory_controller_1 (.in_1(out_4), .D(out_7), .R(out_11), .out_4(memory_controller_1_out_4));
  _12bit_register AR (
    .LD(ar_controller_1_load), .CLR(ar_controller_1_clr), .INR(ar_controller_1_inc), .in_4(n0_12_1_out_2),
    .OUTP(out_8), .CLK(CLK));
  _12bit_register PC (
    .LD(pc_controller_1_load), .CLR(pc_controller_1_clr), .INR(pc_controller_1_inc), .in_4(n0_12_2_out_2),
    .OUTP(out_14), .CLK(CLK));
  _16bit_register DR (
    .in_4(bus_1_out_10), .LD(dr_controller_1_load), .INR(dr_controller_1_inc), .CLR(1'b0), .CLK(CLK),
    .OUTP(out_18));
  DR_Controller dr_controller_1 (.in_1(out_4), .D(out_7), .load(dr_controller_1_load), .inc(dr_controller_1_inc));
  _16bit_register AC (
    .in_4(n16bit_alu_1_out_9), .LD(ac_controller_1_load), .INR(ac_controller_1_inc),
    .CLR(ac_controller_1_clr), .CLK(CLK), .OUTP(out_21));
  _16bit_register IR (
    .in_4(bus_1_out_10), .LD(ir_controller_1_out_3), .INR(ir_controller_1_out_4),
    .CLR(ir_controller_1_out_5), .CLK(CLK), .OUTP(out_6));
  IR_Controller ir_controller_1 (
    .in_1(out_4), .R(out_11), .out_3(ir_controller_1_out_3), .out_4(ir_controller_1_out_4),
    .out_5(ir_controller_1_out_5));
  _16bit_register TR (
    .in_4(bus_1_out_10), .LD(tr_controller_1_out_3), .INR(tr_controller_1_out_4),
    .CLR(tr_controller_1_out_5), .CLK(CLK), .OUTP(out_9));
  TR_Controller tr_controller_1 (
    .in_1(out_4), .R(out_11), .out_3(tr_controller_1_out_3), .out_4(tr_controller_1_out_4),
    .out_5(tr_controller_1_out_5));
  D_Flip_Flop #(.trigger("falling")) d_ff_5 (
    .clk(CLK), .D(fgi_controller_1_out_6), .Q(out_19));  // open: Qn, preset, en, reset
  FGO_Controller fgo_controller_1 (
    .in_1(out_4), .I(out_7), .out_6(fgo_controller_1_out_6), .in_3(out_10), .IR(out_6), .in_5(out_20));
  RAM #(.addrWidth(12), .dataWidth(16), .bus("separate")) ram_1 (
    .addr(out_8), .din(bus_1_out_10), .data(out_5), .str(memory_controller_1_out_4), .clk(CLK), .ld(1'b1));  // open: sel, clr
  D_Flip_Flop #(.trigger("falling")) d_ff_6 (
    .clk(CLK), .D(fgo_controller_1_out_6), .Q(out_20));  // open: Qn, preset, en, reset
  BUS_Controller bus_controller_1 (.T(out_4), .D(out_7), .in_3(out_6), .I(out_10), .R(out_11), .out_6(out_13));
  BUS bus_1 (
    .in_1(out_5), .in_2(out_9), .in_3(out_6), .in_4(out_21), .in_5(out_18), .in_6(out_14), .in_8(in_3),
    .selector(out_13), .out_10(bus_1_out_10), .in_7(out_8));

  // Other names for the same wires on the sheet: AC[15:0] = out_21; AR[11:0] = out_8; BUS[2:0] = out_13;
  //   D[7:0] = out_7; DR[15:0] = out_18; E = out_16; FGI = out_19; FGO = out_20; I = out_10; IEN = out_12;
  //   INPR[7:0] = out_17; IR[15:0] = out_6; M[15:0] = out_5; OUTR[7:0] = out_15; PC[11:0] = out_14; R = out_11;
  //   T[15:0] = out_4; TR[15:0] = out_9
endmodule

module _16bit_incrementer (
  input  [15:0] in_1,
  output [15:0] out_2,
  output out_3
);

  wire and_1_out, and_2_out, and_3_out, and_4_out, and_5_out, and_6_out, and_7_out, and_8_out, and_9_out,
       and_10_out, and_11_out, and_12_out, and_13_out, and_14_out, and_15_out;

  xor xor_1 (out_2[0], 1'b1, in_1[0]);
  and and_1 (and_1_out, in_1[0], 1'b1);
  xor xor_2 (out_2[1], and_1_out, in_1[1]);
  and and_2 (and_2_out, in_1[1], and_1_out);
  xor xor_3 (out_2[2], and_2_out, in_1[2]);
  and and_3 (and_3_out, in_1[2], and_2_out);
  xor xor_4 (out_2[3], and_3_out, in_1[3]);
  and and_4 (and_4_out, in_1[3], and_3_out);
  xor xor_5 (out_2[4], and_4_out, in_1[4]);
  and and_5 (and_5_out, in_1[4], and_4_out);
  xor xor_6 (out_2[5], and_5_out, in_1[5]);
  and and_6 (and_6_out, in_1[5], and_5_out);
  xor xor_7 (out_2[6], and_6_out, in_1[6]);
  and and_7 (and_7_out, in_1[6], and_6_out);
  xor xor_8 (out_2[7], and_7_out, in_1[7]);
  and and_8 (and_8_out, in_1[7], and_7_out);
  xor xor_9 (out_2[8], and_8_out, in_1[8]);
  and and_9 (and_9_out, in_1[8], and_8_out);
  xor xor_10 (out_2[9], and_9_out, in_1[9]);
  and and_10 (and_10_out, in_1[9], and_9_out);
  xor xor_11 (out_2[10], and_10_out, in_1[10]);
  and and_11 (and_11_out, in_1[10], and_10_out);
  xor xor_12 (out_2[11], and_11_out, in_1[11]);
  and and_12 (and_12_out, in_1[11], and_11_out);
  xor xor_13 (out_2[12], and_12_out, in_1[12]);
  and and_13 (and_13_out, in_1[12], and_12_out);
  xor xor_14 (out_2[13], and_13_out, in_1[13]);
  and and_14 (and_14_out, in_1[13], and_13_out);
  xor xor_15 (out_2[14], and_14_out, in_1[14]);
  and and_15 (and_15_out, in_1[14], and_14_out);
  xor xor_16 (out_2[15], and_15_out, in_1[15]);
  and and_16 (out_3, in_1[15], and_15_out);
endmodule

module _16bit_register (
  input  LD,
  input  CLR,
  input  INR,
  input  [15:0] in_4,
  input  CLK,
  output [15:0] OUTP
);

  wire and_3_out, and_4_out, and_5_out, and_6_out, and_7_out, and_8_out, and_9_out, and_10_out, and_11_out,
       and_12_out, and_13_out, and_14_out, and_15_out, and_16_out, and_17_out, and_18_out, and_19_out,
       and_20_out, and_21_out, and_22_out, and_23_out, and_24_out, and_25_out, and_26_out, and_27_out,
       and_28_out, and_29_out, and_30_out, and_31_out, and_32_out, and_33_out, and_34_out, not_2_out,
       not_3_out, or_1_out, or_3_out, or_4_out, or_5_out, or_6_out, or_7_out, or_8_out, or_9_out, or_10_out,
       or_11_out, or_12_out, or_13_out, or_14_out, or_15_out, or_16_out, or_17_out, or_18_out;
  wire [15:0] and_1_out, and_2_out, n16bit_incrementer_1_out_2, not_1_out, or_2_out;

  _16bit_incrementer u_16bit_incrementer_1 (.in_1(OUTP), .out_2(n16bit_incrementer_1_out_2));  // open: out_3
  or or_1 (or_1_out, LD, INR);
  assign and_1_out = n16bit_incrementer_1_out_2 & {16{INR}};  // AND_Gate and_1, 16 bits wide
  assign not_1_out = ~{16{INR}};  // NOT_Gate not_1, 16 bits wide
  assign and_2_out = not_1_out & in_4;  // AND_Gate and_2, 16 bits wide
  assign or_2_out = and_1_out | and_2_out;  // OR_Gate or_2, 16 bits wide
  not not_2 (not_2_out, or_1_out);
  not not_3 (not_3_out, not_2_out);
  and and_3 (and_3_out, OUTP[0], not_2_out);
  and and_4 (and_4_out, or_2_out[0], not_3_out);
  and and_5 (and_5_out, OUTP[1], not_2_out);
  and and_6 (and_6_out, or_2_out[1], not_3_out);
  and and_7 (and_7_out, OUTP[2], not_2_out);
  and and_8 (and_8_out, or_2_out[2], not_3_out);
  and and_9 (and_9_out, OUTP[3], not_2_out);
  and and_10 (and_10_out, or_2_out[3], not_3_out);
  and and_11 (and_11_out, OUTP[4], not_2_out);
  and and_12 (and_12_out, or_2_out[4], not_3_out);
  and and_13 (and_13_out, OUTP[5], not_2_out);
  and and_14 (and_14_out, or_2_out[5], not_3_out);
  and and_15 (and_15_out, OUTP[6], not_2_out);
  and and_16 (and_16_out, or_2_out[6], not_3_out);
  and and_17 (and_17_out, OUTP[7], not_2_out);
  and and_18 (and_18_out, or_2_out[7], not_3_out);
  and and_19 (and_19_out, OUTP[8], not_2_out);
  and and_20 (and_20_out, or_2_out[8], not_3_out);
  and and_21 (and_21_out, OUTP[9], not_2_out);
  and and_22 (and_22_out, or_2_out[9], not_3_out);
  and and_23 (and_23_out, OUTP[10], not_2_out);
  and and_24 (and_24_out, or_2_out[10], not_3_out);
  and and_25 (and_25_out, OUTP[11], not_2_out);
  and and_26 (and_26_out, or_2_out[11], not_3_out);
  and and_27 (and_27_out, OUTP[12], not_2_out);
  and and_28 (and_28_out, or_2_out[12], not_3_out);
  and and_29 (and_29_out, OUTP[13], not_2_out);
  and and_30 (and_30_out, or_2_out[13], not_3_out);
  and and_31 (and_31_out, OUTP[14], not_2_out);
  and and_32 (and_32_out, or_2_out[14], not_3_out);
  and and_33 (and_33_out, OUTP[15], not_2_out);
  and and_34 (and_34_out, or_2_out[15], not_3_out);
  or or_3 (or_3_out, and_3_out, and_4_out);
  or or_4 (or_4_out, and_5_out, and_6_out);
  or or_5 (or_5_out, and_7_out, and_8_out);
  or or_6 (or_6_out, and_9_out, and_10_out);
  or or_7 (or_7_out, and_11_out, and_12_out);
  or or_8 (or_8_out, and_13_out, and_14_out);
  or or_9 (or_9_out, and_15_out, and_16_out);
  or or_10 (or_10_out, and_17_out, and_18_out);
  or or_11 (or_11_out, and_19_out, and_20_out);
  or or_12 (or_12_out, and_21_out, and_22_out);
  or or_13 (or_13_out, and_23_out, and_24_out);
  or or_14 (or_14_out, and_25_out, and_26_out);
  or or_15 (or_15_out, and_27_out, and_28_out);
  or or_16 (or_16_out, and_29_out, and_30_out);
  or or_17 (or_17_out, and_31_out, and_32_out);
  or or_18 (or_18_out, and_33_out, and_34_out);
  D_Flip_Flop #(.trigger("falling")) d_ff_1 (
    .clk(CLK), .D(or_3_out), .Q(OUTP[0]), .reset(CLR));  // open: Qn, preset, en
  D_Flip_Flop #(.trigger("falling")) d_ff_2 (
    .clk(CLK), .D(or_4_out), .Q(OUTP[1]), .reset(CLR));  // open: Qn, preset, en
  D_Flip_Flop #(.trigger("falling")) d_ff_3 (
    .clk(CLK), .D(or_5_out), .Q(OUTP[2]), .reset(CLR));  // open: Qn, preset, en
  D_Flip_Flop #(.trigger("falling")) d_ff_4 (
    .clk(CLK), .D(or_6_out), .Q(OUTP[3]), .reset(CLR));  // open: Qn, preset, en
  D_Flip_Flop #(.trigger("falling")) d_ff_5 (
    .clk(CLK), .D(or_7_out), .Q(OUTP[4]), .reset(CLR));  // open: Qn, preset, en
  D_Flip_Flop #(.trigger("falling")) d_ff_6 (
    .clk(CLK), .D(or_8_out), .Q(OUTP[5]), .reset(CLR));  // open: Qn, preset, en
  D_Flip_Flop #(.trigger("falling")) d_ff_7 (
    .clk(CLK), .D(or_9_out), .Q(OUTP[6]), .reset(CLR));  // open: Qn, preset, en
  D_Flip_Flop #(.trigger("falling")) d_ff_8 (
    .clk(CLK), .D(or_10_out), .Q(OUTP[7]), .reset(CLR));  // open: Qn, preset, en
  D_Flip_Flop #(.trigger("falling")) d_ff_9 (
    .clk(CLK), .D(or_11_out), .Q(OUTP[8]), .reset(CLR));  // open: Qn, preset, en
  D_Flip_Flop #(.trigger("falling")) d_ff_10 (
    .clk(CLK), .D(or_12_out), .Q(OUTP[9]), .reset(CLR));  // open: Qn, preset, en
  D_Flip_Flop #(.trigger("falling")) d_ff_11 (
    .clk(CLK), .D(or_13_out), .Q(OUTP[10]), .reset(CLR));  // open: Qn, preset, en
  D_Flip_Flop #(.trigger("falling")) d_ff_12 (
    .clk(CLK), .D(or_14_out), .Q(OUTP[11]), .reset(CLR));  // open: Qn, preset, en
  D_Flip_Flop #(.trigger("falling")) d_ff_13 (
    .clk(CLK), .D(or_15_out), .Q(OUTP[12]), .reset(CLR));  // open: Qn, preset, en
  D_Flip_Flop #(.trigger("falling")) d_ff_14 (
    .clk(CLK), .D(or_16_out), .Q(OUTP[13]), .reset(CLR));  // open: Qn, preset, en
  D_Flip_Flop #(.trigger("falling")) d_ff_15 (
    .clk(CLK), .D(or_17_out), .Q(OUTP[14]), .reset(CLR));  // open: Qn, preset, en
  D_Flip_Flop #(.trigger("falling")) d_ff_16 (
    .clk(CLK), .D(or_18_out), .Q(OUTP[15]), .reset(CLR));  // open: Qn, preset, en

  // Other names for the same wires on the sheet: INC[15:0] = {16{INR}}; OUT[15:0] = OUTP

  // Notes on the sheet:
  //   INP
endmodule

module _12bit_register (
  input  LD,
  input  CLR,
  input  INR,
  input  [11:0] in_4,
  input  CLK,
  output [11:0] OUTP
);

  wire and_3_out, and_4_out, and_5_out, and_6_out, and_7_out, and_8_out, and_9_out, and_10_out, and_11_out,
       and_12_out, and_13_out, and_14_out, and_15_out, and_16_out, and_17_out, and_18_out, and_19_out,
       and_20_out, and_21_out, and_22_out, and_23_out, and_24_out, and_25_out, and_26_out, not_2_out,
       not_3_out, or_1_out, or_3_out, or_4_out, or_5_out, or_6_out, or_7_out, or_8_out, or_9_out, or_10_out,
       or_11_out, or_12_out, or_13_out, or_14_out;
  wire [11:0] and_1_out, and_2_out, not_1_out, or_2_out;
  wire [15:0] n16bit_incrementer_1_out_2;

  _16bit_incrementer u_16bit_incrementer_1 (.in_1({4'b0000, OUTP}), .out_2(n16bit_incrementer_1_out_2));  // open: out_3
  or or_1 (or_1_out, LD, INR);
  assign not_1_out = ~{12{INR}};  // NOT_Gate not_1, 12 bits wide
  assign and_1_out = n16bit_incrementer_1_out_2[11:0] & {12{INR}};  // AND_Gate and_1, 12 bits wide
  assign or_2_out = and_1_out | and_2_out;  // OR_Gate or_2, 12 bits wide
  assign and_2_out = not_1_out & in_4;  // AND_Gate and_2, 12 bits wide
  not not_2 (not_2_out, or_1_out);
  not not_3 (not_3_out, not_2_out);
  and and_3 (and_3_out, OUTP[0], not_2_out);
  and and_4 (and_4_out, or_2_out[0], not_3_out);
  and and_5 (and_5_out, OUTP[1], not_2_out);
  and and_6 (and_6_out, or_2_out[1], not_3_out);
  and and_7 (and_7_out, OUTP[2], not_2_out);
  and and_8 (and_8_out, or_2_out[2], not_3_out);
  and and_9 (and_9_out, OUTP[3], not_2_out);
  and and_10 (and_10_out, or_2_out[3], not_3_out);
  and and_11 (and_11_out, OUTP[4], not_2_out);
  and and_12 (and_12_out, or_2_out[4], not_3_out);
  and and_13 (and_13_out, OUTP[5], not_2_out);
  and and_14 (and_14_out, or_2_out[5], not_3_out);
  and and_15 (and_15_out, OUTP[6], not_2_out);
  and and_16 (and_16_out, or_2_out[6], not_3_out);
  and and_17 (and_17_out, OUTP[7], not_2_out);
  and and_18 (and_18_out, or_2_out[7], not_3_out);
  and and_19 (and_19_out, OUTP[8], not_2_out);
  and and_20 (and_20_out, or_2_out[8], not_3_out);
  and and_21 (and_21_out, OUTP[9], not_2_out);
  and and_22 (and_22_out, or_2_out[9], not_3_out);
  and and_23 (and_23_out, OUTP[10], not_2_out);
  and and_24 (and_24_out, or_2_out[10], not_3_out);
  and and_25 (and_25_out, OUTP[11], not_2_out);
  and and_26 (and_26_out, or_2_out[11], not_3_out);
  or or_3 (or_3_out, and_3_out, and_4_out);
  or or_4 (or_4_out, and_5_out, and_6_out);
  or or_5 (or_5_out, and_7_out, and_8_out);
  or or_6 (or_6_out, and_9_out, and_10_out);
  or or_7 (or_7_out, and_11_out, and_12_out);
  or or_8 (or_8_out, and_13_out, and_14_out);
  or or_9 (or_9_out, and_15_out, and_16_out);
  or or_10 (or_10_out, and_17_out, and_18_out);
  or or_11 (or_11_out, and_19_out, and_20_out);
  or or_12 (or_12_out, and_21_out, and_22_out);
  or or_13 (or_13_out, and_23_out, and_24_out);
  or or_14 (or_14_out, and_25_out, and_26_out);
  D_Flip_Flop #(.trigger("falling")) d_ff_1 (
    .clk(CLK), .D(or_3_out), .Q(OUTP[0]), .reset(CLR));  // open: Qn, preset, en
  D_Flip_Flop #(.trigger("falling")) d_ff_2 (
    .clk(CLK), .D(or_4_out), .Q(OUTP[1]), .reset(CLR));  // open: Qn, preset, en
  D_Flip_Flop #(.trigger("falling")) d_ff_3 (
    .clk(CLK), .D(or_5_out), .Q(OUTP[2]), .reset(CLR));  // open: Qn, preset, en
  D_Flip_Flop #(.trigger("falling")) d_ff_4 (
    .clk(CLK), .D(or_6_out), .Q(OUTP[3]), .reset(CLR));  // open: Qn, preset, en
  D_Flip_Flop #(.trigger("falling")) d_ff_5 (
    .clk(CLK), .D(or_7_out), .Q(OUTP[4]), .reset(CLR));  // open: Qn, preset, en
  D_Flip_Flop #(.trigger("falling")) d_ff_6 (
    .clk(CLK), .D(or_8_out), .Q(OUTP[5]), .reset(CLR));  // open: Qn, preset, en
  D_Flip_Flop #(.trigger("falling")) d_ff_7 (
    .clk(CLK), .D(or_9_out), .Q(OUTP[6]), .reset(CLR));  // open: Qn, preset, en
  D_Flip_Flop #(.trigger("falling")) d_ff_8 (
    .clk(CLK), .D(or_10_out), .Q(OUTP[7]), .reset(CLR));  // open: Qn, preset, en
  D_Flip_Flop #(.trigger("falling")) d_ff_9 (
    .clk(CLK), .D(or_11_out), .Q(OUTP[8]), .reset(CLR));  // open: Qn, preset, en
  D_Flip_Flop #(.trigger("falling")) d_ff_10 (
    .clk(CLK), .D(or_12_out), .Q(OUTP[9]), .reset(CLR));  // open: Qn, preset, en
  D_Flip_Flop #(.trigger("falling")) d_ff_11 (
    .clk(CLK), .D(or_13_out), .Q(OUTP[10]), .reset(CLR));  // open: Qn, preset, en
  D_Flip_Flop #(.trigger("falling")) d_ff_12 (
    .clk(CLK), .D(or_14_out), .Q(OUTP[11]), .reset(CLR));  // open: Qn, preset, en

  // Other names for the same wires on the sheet: INC[11:0] = {12{INR}}; OUT[11:0] = OUTP

  // Notes on the sheet:
  //   INP
endmodule

module _8bit_register (
  input  LD,
  input  CLR,
  input  INR,
  input  CLK,
  input  [7:0] in_5,
  output [7:0] OUTP
);

  wire and_3_out, and_4_out, and_5_out, and_6_out, and_7_out, and_8_out, and_9_out, and_10_out, and_11_out,
       and_12_out, and_13_out, and_14_out, and_15_out, and_16_out, and_17_out, and_18_out, not_2_out,
       not_3_out, or_1_out, or_3_out, or_4_out, or_5_out, or_6_out, or_7_out, or_8_out, or_9_out, or_10_out;
  wire [7:0] and_1_out, and_2_out, not_1_out, or_2_out;
  wire [15:0] n16bit_incrementer_1_out_2;

  _16bit_incrementer u_16bit_incrementer_1 (
    .in_1({{8{1'b0}}, OUTP}), .out_2(n16bit_incrementer_1_out_2));  // open: out_3
  or or_1 (or_1_out, LD, INR);
  assign not_1_out = ~{8{INR}};  // NOT_Gate not_1, 8 bits wide
  assign and_1_out = n16bit_incrementer_1_out_2[7:0] & {8{INR}};  // AND_Gate and_1, 8 bits wide
  assign or_2_out = and_1_out | and_2_out;  // OR_Gate or_2, 8 bits wide
  assign and_2_out = not_1_out & in_5;  // AND_Gate and_2, 8 bits wide
  not not_2 (not_2_out, or_1_out);
  not not_3 (not_3_out, not_2_out);
  and and_3 (and_3_out, OUTP[0], not_2_out);
  and and_4 (and_4_out, or_2_out[0], not_3_out);
  and and_5 (and_5_out, OUTP[1], not_2_out);
  and and_6 (and_6_out, or_2_out[1], not_3_out);
  and and_7 (and_7_out, OUTP[2], not_2_out);
  and and_8 (and_8_out, or_2_out[2], not_3_out);
  and and_9 (and_9_out, OUTP[3], not_2_out);
  and and_10 (and_10_out, or_2_out[3], not_3_out);
  and and_11 (and_11_out, OUTP[4], not_2_out);
  and and_12 (and_12_out, or_2_out[4], not_3_out);
  and and_13 (and_13_out, OUTP[5], not_2_out);
  and and_14 (and_14_out, or_2_out[5], not_3_out);
  and and_15 (and_15_out, OUTP[6], not_2_out);
  and and_16 (and_16_out, or_2_out[6], not_3_out);
  and and_17 (and_17_out, OUTP[7], not_2_out);
  and and_18 (and_18_out, or_2_out[7], not_3_out);
  or or_3 (or_3_out, and_3_out, and_4_out);
  or or_4 (or_4_out, and_5_out, and_6_out);
  or or_5 (or_5_out, and_7_out, and_8_out);
  or or_6 (or_6_out, and_9_out, and_10_out);
  or or_7 (or_7_out, and_11_out, and_12_out);
  or or_8 (or_8_out, and_13_out, and_14_out);
  or or_9 (or_9_out, and_15_out, and_16_out);
  or or_10 (or_10_out, and_17_out, and_18_out);
  D_Flip_Flop #(.trigger("falling")) d_ff_1 (
    .clk(CLK), .D(or_3_out), .Q(OUTP[0]), .reset(CLR));  // open: Qn, preset, en
  D_Flip_Flop #(.trigger("falling")) d_ff_2 (
    .clk(CLK), .D(or_4_out), .Q(OUTP[1]), .reset(CLR));  // open: Qn, preset, en
  D_Flip_Flop #(.trigger("falling")) d_ff_3 (
    .clk(CLK), .D(or_5_out), .Q(OUTP[2]), .reset(CLR));  // open: Qn, preset, en
  D_Flip_Flop #(.trigger("falling")) d_ff_4 (
    .clk(CLK), .D(or_6_out), .Q(OUTP[3]), .reset(CLR));  // open: Qn, preset, en
  D_Flip_Flop #(.trigger("falling")) d_ff_5 (
    .clk(CLK), .D(or_7_out), .Q(OUTP[4]), .reset(CLR));  // open: Qn, preset, en
  D_Flip_Flop #(.trigger("falling")) d_ff_6 (
    .clk(CLK), .D(or_8_out), .Q(OUTP[5]), .reset(CLR));  // open: Qn, preset, en
  D_Flip_Flop #(.trigger("falling")) d_ff_7 (
    .clk(CLK), .D(or_9_out), .Q(OUTP[6]), .reset(CLR));  // open: Qn, preset, en
  D_Flip_Flop #(.trigger("falling")) d_ff_8 (
    .clk(CLK), .D(or_10_out), .Q(OUTP[7]), .reset(CLR));  // open: Qn, preset, en

  // Other names for the same wires on the sheet: INC[7:0] = {8{INR}}; OUT[7:0] = OUTP

  // Notes on the sheet:
  //   INP
endmodule

module BUS (
  input  [15:0] in_1,
  input  [15:0] in_2,
  input  [15:0] in_3,
  input  [15:0] in_4,
  input  [15:0] in_5,
  input  [11:0] in_6,
  input  [11:0] in_7,
  input  [15:0] in_8,
  input  [2:0] selector,
  output [15:0] out_10
);

  wire decoder_1_out0, decoder_1_out1, decoder_1_out2, decoder_1_out3, decoder_1_out4, decoder_1_out5,
       decoder_1_out6, decoder_1_out7;

  assign out_10 = decoder_1_out2 ? {4'b0000, in_6} : 16'bz;  // Controlled_Buffer controlled_buffer_1
  assign out_10 = decoder_1_out1 ? {4'b0000, in_7} : 16'bz;  // Controlled_Buffer controlled_buffer_2
  assign out_10 = decoder_1_out0 ? in_8 : 16'bz;  // Controlled_Buffer controlled_buffer_3
  Decoder #(.select(3)) decoder_1 (
    .out0(decoder_1_out0), .out1(decoder_1_out1), .out2(decoder_1_out2), .out3(decoder_1_out3),
    .out4(decoder_1_out4), .out5(decoder_1_out5), .out6(decoder_1_out6), .out7(decoder_1_out7), .sel(selector));  // open: en
  assign out_10 = decoder_1_out6 ? in_2 : 16'bz;  // Controlled_Buffer controlled_buffer_4
  assign out_10 = decoder_1_out5 ? in_3 : 16'bz;  // Controlled_Buffer controlled_buffer_5
  assign out_10 = decoder_1_out4 ? in_4 : 16'bz;  // Controlled_Buffer controlled_buffer_6
  assign out_10 = decoder_1_out3 ? in_5 : 16'bz;  // Controlled_Buffer controlled_buffer_7
  assign out_10 = decoder_1_out7 ? in_1 : 16'bz;  // Controlled_Buffer controlled_buffer_8

  // Notes on the sheet:
  //   I0-I7
endmodule

module _0_8 (
  input  [15:0] in_1,
  output [7:0] out_2
);


  assign out_2 = in_1[7:0];
endmodule

module _0_12 (
  input  [15:0] in_1,
  output [11:0] out_2
);


  assign out_2 = in_1[11:0];
endmodule

module SC (
  input  count_enable,
  input  CLK,
  input  clr,
  output [15:0] out_4
);

  wire and_1_out, and_2_out, and_3_out, and_4_out, and_5_out, and_6_out, and_7_out, not_1_out, or_1_out,
       or_2_out, or_3_out, or_4_out;
  wire [3:0] j_k_ff_1_q;

  not not_1 (not_1_out, clr);
  and and_1 (and_1_out, count_enable, j_k_ff_1_q[0]);
  and and_2 (and_2_out, and_1_out, j_k_ff_1_q[1]);
  and and_3 (and_3_out, and_2_out, j_k_ff_1_q[2]);
  and and_4 (and_4_out, not_1_out, count_enable);
  or or_1 (or_1_out, count_enable, clr);
  and and_5 (and_5_out, not_1_out, and_1_out);
  or or_2 (or_2_out, and_1_out, clr);
  and and_6 (and_6_out, not_1_out, and_2_out);
  or or_3 (or_3_out, and_2_out, clr);
  and and_7 (and_7_out, not_1_out, and_3_out);
  or or_4 (or_4_out, and_3_out, clr);
  J_K_Flip_Flop #(.trigger("falling")) j_k_ff_1 (
    .J(and_4_out), .clk(CLK), .K(or_1_out), .Q(j_k_ff_1_q[0]));  // open: Qn, preset, en, reset
  J_K_Flip_Flop #(.trigger("falling")) j_k_ff_2 (
    .J(and_5_out), .clk(CLK), .K(or_2_out), .Q(j_k_ff_1_q[1]));  // open: Qn, preset, en, reset
  J_K_Flip_Flop #(.trigger("falling")) j_k_ff_3 (
    .J(and_6_out), .clk(CLK), .K(or_3_out), .Q(j_k_ff_1_q[2]));  // open: Qn, preset, en, reset
  J_K_Flip_Flop #(.trigger("falling")) j_k_ff_4 (
    .J(and_7_out), .clk(CLK), .K(or_4_out), .Q(j_k_ff_1_q[3]));  // open: Qn, preset, en, reset
  Decoder #(.select(4)) decoder_1 (
    .out0(out_4[0]), .out1(out_4[1]), .out2(out_4[2]), .out3(out_4[3]), .out4(out_4[4]), .out5(out_4[5]),
    .out6(out_4[6]), .out7(out_4[7]), .out8(out_4[8]), .out9(out_4[9]), .out10(out_4[10]), .out11(out_4[11]),
    .out12(out_4[12]), .out13(out_4[13]), .out14(out_4[14]), .out15(out_4[15]), .sel(j_k_ff_1_q), .en(1'b1));
endmodule

module IR_Decoder (
  input  [15:0] in_1,
  output [7:0] out_2,
  output out_3
);

  Decoder #(.select(3)) decoder_1 (
    .out0(out_2[0]), .out1(out_2[1]), .out2(out_2[2]), .out3(out_2[3]), .out4(out_2[4]), .out5(out_2[5]),
    .out6(out_2[6]), .out7(out_2[7]), .sel(in_1[14:12]));  // open: en

  assign out_3 = in_1[15];
endmodule

module R_Controller (
  input  [15:0] in_1,
  input  IEN,
  input  FGO,
  input  FGI,
  input  R,
  output out_6
);

  wire and_1_out, and_2_out, and_3_out, not_1_out, not_2_out, not_3_out, not_4_out, or_1_out;

  or or_1 (or_1_out, FGO, FGI);
  not not_1 (not_1_out, in_1[2]);
  not not_2 (not_2_out, in_1[1]);
  not not_3 (not_3_out, in_1[0]);
  not not_4 (not_4_out, and_1_out);
  and and_1 (and_1_out, in_1[2], R);
  and and_2 (and_2_out, not_3_out, not_2_out, not_1_out, IEN, or_1_out);
  and and_3 (and_3_out, R, not_4_out);
  or or_2 (out_6, and_2_out, and_3_out);

  // Notes on the sheet:
  //   T
endmodule

module FGO_Controller (
  input  [15:0] in_1,
  input  [7:0] I,
  input  in_3,
  input  [15:0] IR,
  input  in_5,
  output out_6
);

  wire and_1_out, and_2_out, not_1_out;

  and and_1 (and_1_out, in_1[3], I[7], in_3);
  and and_2 (and_2_out, and_1_out, IR[11]);
  not not_1 (not_1_out, and_2_out);
  and and_3 (out_6, not_1_out, in_5);

  // Notes on the sheet:
  //   T
  //   D
endmodule

module FGI_Controller (
  input  [15:0] in_1,
  input  [7:0] I,
  input  in_3,
  input  [15:0] IR,
  input  in_5,
  output out_6
);

  wire and_1_out, and_2_out, not_1_out;

  and and_1 (and_1_out, in_1[3], I[7], in_3);
  and and_2 (and_2_out, and_1_out, IR[11]);
  not not_1 (not_1_out, and_2_out);
  and and_3 (out_6, not_1_out, in_5);

  // Notes on the sheet:
  //   T
  //   D
endmodule

module IEN_Controller (
  input  [15:0] in_1,
  input  [7:0] D,
  input  I,
  input  [15:0] IR,
  input  R,
  input  IEN,
  output out_7
);

  wire and_1_out, and_2_out, and_3_out, and_4_out, and_5_out, not_1_out, or_1_out;

  and and_1 (and_1_out, in_1[3], D[7], I);
  and and_2 (and_2_out, and_1_out, IR[6]);
  and and_3 (and_3_out, and_1_out, IR[7]);
  and and_4 (and_4_out, in_1[2], R);
  or or_1 (or_1_out, and_2_out, and_4_out);
  not not_1 (not_1_out, or_1_out);
  and and_5 (and_5_out, IEN, not_1_out);
  or or_2 (out_7, and_5_out, and_3_out);

  // Notes on the sheet:
  //   T
endmodule

module Memory_Controller (
  input  [15:0] in_1,
  input  [7:0] D,
  input  R,
  output out_4
);

  wire and_1_out, and_2_out, and_3_out, and_4_out;

  and and_1 (and_1_out, in_1[6], D[6]);
  and and_2 (and_2_out, in_1[4], D[3]);
  and and_3 (and_3_out, D[5], in_1[4]);
  and and_4 (and_4_out, in_1[1], R);
  or or_1 (out_4, and_1_out, and_2_out, and_3_out, and_4_out);

  // Notes on the sheet:
  //   T
endmodule

module AR_Controller (
  input  [15:0] in_1,
  input  [7:0] D,
  input  I,
  input  R,
  output load,
  output inc,
  output clr
);

  wire and_1_out, and_2_out, and_3_out, not_1_out, not_2_out;

  not not_1 (not_1_out, R);
  not not_2 (not_2_out, D[7]);
  and and_1 (and_1_out, in_1[0], not_1_out);
  and and_2 (and_2_out, in_1[2], not_1_out);
  and and_3 (and_3_out, in_1[3], not_2_out, I);
  and and_4 (inc, in_1[4], D[5]);
  and and_5 (clr, in_1[0], R);
  or or_1 (load, and_1_out, and_2_out, and_3_out);

  // Notes on the sheet:
  //   T
endmodule

module PC_Controller (
  input  [15:0] in_1,
  input  [7:0] D,
  input  [15:0] in_3,
  input  [15:0] in_4,
  input  [15:0] IR,
  input  I,
  input  R,
  input  E,
  input  FGO,
  input  FGI,
  output inc,
  output load,
  output clr
);

  wire and_1_out, and_2_out, and_3_out, and_4_out, and_5_out, and_6_out, and_7_out, and_8_out, and_9_out,
       and_10_out, and_11_out, and_12_out, not_1_out, not_2_out, not_3_out, not_4_out, not_5_out, not_6_out,
       or_1_out, or_2_out;

  not not_1 (not_1_out, I);
  not not_2 (not_2_out, R);
  not not_3 (not_3_out, E);
  or or_1 (or_1_out, in_3[0], in_3[1], in_3[2], in_3[3], in_3[4], in_3[5], in_3[6], in_3[7], in_3[8], in_3[9], in_3[10], in_3[11], in_3[12], in_3[13], in_3[14], in_3[15]);
  or or_2 (or_2_out, in_4[0], in_4[1], in_4[2], in_4[3], in_4[4], in_4[5], in_4[6], in_4[7], in_4[8], in_4[9], in_4[10], in_4[11], in_4[12], in_4[13], in_4[14], in_4[15]);
  not not_4 (not_4_out, or_1_out);
  not not_5 (not_5_out, or_2_out);
  and and_1 (and_1_out, D[7], in_1[3]);
  not not_6 (not_6_out, in_3[15]);
  and and_2 (and_2_out, in_1[1], not_2_out);
  and and_3 (and_3_out, in_1[2], R);
  and and_4 (and_4_out, in_1[6], not_5_out, D[6]);
  and and_5 (and_5_out, and_1_out, not_1_out, IR[4], not_6_out);
  and and_6 (and_6_out, and_1_out, not_1_out, IR[3], in_3[15]);
  and and_7 (and_7_out, and_1_out, not_1_out, IR[2], not_4_out);
  and and_8 (and_8_out, and_1_out, not_2_out, IR[1], not_3_out);
  and and_9 (and_9_out, and_1_out, I, IR[8], FGO);
  and and_10 (and_10_out, and_1_out, I, IR[9], FGI);
  and and_11 (and_11_out, in_1[4], D[4]);
  and and_12 (and_12_out, in_1[5], D[5]);
  and and_13 (clr, in_1[1], R);
  or or_3 (load, and_11_out, and_12_out);
  or or_4 (inc, and_2_out, and_3_out, and_4_out, and_5_out, and_6_out, and_7_out, and_8_out, and_9_out, and_10_out);

  // Notes on the sheet:
  //   T
  //   AC
  //   DR
endmodule

module DR_Controller (
  input  [15:0] in_1,
  input  [7:0] D,
  output load,
  output inc
);

  wire and_1_out, and_2_out, and_3_out, and_4_out;

  and and_1 (and_1_out, in_1[4], D[0]);
  and and_2 (and_2_out, in_1[4], D[1]);
  and and_3 (and_3_out, in_1[4], D[2]);
  and and_4 (and_4_out, in_1[4], D[6]);
  and and_5 (inc, in_1[5], D[6]);
  or or_1 (load, and_1_out, and_2_out, and_3_out, and_4_out);

  // Notes on the sheet:
  //   T
endmodule

module ALU (
  input  [15:0] in_1,
  input  [7:0] D,
  input  [15:0] IR,
  input  I,
  input  [2:0] DR,
  input  INPR,
  input  C,
  input  in_8,
  output out_9,
  output out_10
);

  wire and_1_out, and_2_out, and_3_out, and_4_out, and_5_out, and_6_out, and_7_out, and_8_out, and_9_out,
       and_10_out, and_11_out, and_12_out, and_13_out, and_14_out, and_15_out, n1bit_adder_1_out_4,
       not_1_out, not_2_out;

  not not_1 (not_1_out, I);
  and and_1 (and_1_out, D[7], in_1[3]);
  and and_2 (and_2_out, in_1[5], D[0]);
  and and_3 (and_3_out, in_1[5], D[1]);
  and and_4 (and_4_out, in_1[5], D[2]);
  and and_5 (and_5_out, and_1_out, IR[11], I);
  and and_6 (and_6_out, and_1_out, not_1_out, IR[9]);
  and and_7 (and_7_out, and_1_out, not_1_out, IR[7]);
  and and_8 (and_8_out, and_1_out, not_1_out, IR[6]);
  not not_2 (not_2_out, DR[1]);
  and and_9 (and_9_out, and_2_out, INPR, DR[1]);
  and and_10 (and_10_out, and_3_out, n1bit_adder_1_out_4);
  _1bit_adder u_1bit_adder_1 (.a(DR[1]), .b(INPR), .c(in_8), .out_4(n1bit_adder_1_out_4), .Cout(out_10));
  and and_11 (and_11_out, and_4_out, INPR);
  and and_12 (and_12_out, and_5_out, C);
  and and_13 (and_13_out, and_6_out, not_2_out);
  and and_14 (and_14_out, and_7_out, DR[2]);
  and and_15 (and_15_out, and_8_out, DR[0]);
  or or_1 (out_9, and_9_out, and_10_out, and_11_out, and_12_out, and_13_out, and_14_out, and_15_out);

  // Notes on the sheet:
  //   T
  //   AC[i-1, i+1]
endmodule

module _1bit_adder (
  input  a,
  input  b,
  input  c,
  output out_4,
  output Cout
);

  wire and_1_out, and_2_out, xor_1_out;

  xor xor_1 (xor_1_out, a, b);
  and and_1 (and_1_out, a, b);
  xor xor_2 (out_4, xor_1_out, c);
  and and_2 (and_2_out, xor_1_out, c);
  or or_1 (Cout, and_2_out, and_1_out);
endmodule

module _16bit_ALU (
  input  E,
  input  [15:0] T,
  input  [7:0] INPR,
  input  [7:0] D,
  input  [15:0] in_5,
  input  [15:0] IR,
  input  [15:0] in_7,
  input  I,
  output [15:0] out_9,
  output E_2
);

  wire alu_1_out_10, alu_2_out_10, alu_3_out_10, alu_4_out_10, alu_5_out_10, alu_6_out_10, alu_7_out_10,
       alu_8_out_10, alu_9_out_10, alu_10_out_10, alu_11_out_10, alu_12_out_10, alu_13_out_10, alu_14_out_10,
       alu_15_out_10, alu_16_out_10, and_1_out, and_2_out, and_3_out, and_4_out, and_5_out;

  and and_1 (and_1_out, T[3], D[7]);
  and and_2 (and_2_out, and_1_out, IR[6]);
  and and_3 (and_3_out, IR[7], and_1_out);
  ALU alu_1 (
    .in_1(T), .D(D), .IR(IR), .I(I), .DR({in_7[1:0], E}), .INPR(in_5[0]), .C(INPR[0]), .in_8(1'b0),
    .out_9(out_9[0]), .out_10(alu_1_out_10));
  ALU alu_2 (
    .in_1(T), .D(D), .IR(IR), .I(I), .DR(in_7[2:0]), .INPR(in_5[1]), .C(INPR[1]), .in_8(alu_1_out_10),
    .out_9(out_9[1]), .out_10(alu_2_out_10));
  ALU alu_3 (
    .in_1(T), .D(D), .IR(IR), .I(I), .DR(in_7[3:1]), .INPR(in_5[2]), .C(INPR[2]), .in_8(alu_2_out_10),
    .out_9(out_9[2]), .out_10(alu_3_out_10));
  ALU alu_4 (
    .in_1(T), .D(D), .IR(IR), .I(I), .DR(in_7[4:2]), .INPR(in_5[3]), .C(INPR[3]), .in_8(alu_3_out_10),
    .out_9(out_9[3]), .out_10(alu_4_out_10));
  ALU alu_5 (
    .in_1(T), .D(D), .IR(IR), .I(I), .DR(in_7[5:3]), .INPR(in_5[4]), .C(INPR[4]), .in_8(alu_4_out_10),
    .out_9(out_9[4]), .out_10(alu_5_out_10));
  ALU alu_6 (
    .in_1(T), .D(D), .IR(IR), .I(I), .DR(in_7[6:4]), .INPR(in_5[5]), .C(INPR[5]), .in_8(alu_5_out_10),
    .out_9(out_9[5]), .out_10(alu_6_out_10));
  ALU alu_7 (
    .in_1(T), .D(D), .IR(IR), .I(I), .DR(in_7[7:5]), .INPR(in_5[6]), .C(INPR[6]), .in_8(alu_6_out_10),
    .out_9(out_9[6]), .out_10(alu_7_out_10));
  ALU alu_8 (
    .in_1(T), .D(D), .IR(IR), .I(I), .DR(in_7[8:6]), .INPR(in_5[7]), .C(INPR[7]), .in_8(alu_7_out_10),
    .out_9(out_9[7]), .out_10(alu_8_out_10));
  ALU alu_9 (
    .in_1(T), .D(D), .IR(IR), .I(I), .DR(in_7[9:7]), .INPR(in_5[8]), .C(1'b0), .in_8(alu_8_out_10),
    .out_9(out_9[8]), .out_10(alu_9_out_10));
  ALU alu_10 (
    .in_1(T), .D(D), .IR(IR), .I(I), .DR(in_7[10:8]), .INPR(in_5[9]), .C(1'b0), .in_8(alu_9_out_10),
    .out_9(out_9[9]), .out_10(alu_10_out_10));
  ALU alu_11 (
    .in_1(T), .D(D), .IR(IR), .I(I), .DR(in_7[11:9]), .INPR(in_5[10]), .C(1'b0), .in_8(alu_10_out_10),
    .out_9(out_9[10]), .out_10(alu_11_out_10));
  ALU alu_12 (
    .in_1(T), .D(D), .IR(IR), .I(I), .DR(in_7[12:10]), .INPR(in_5[11]), .C(1'b0), .in_8(alu_11_out_10),
    .out_9(out_9[11]), .out_10(alu_12_out_10));
  ALU alu_13 (
    .in_1(T), .D(D), .IR(IR), .I(I), .DR(in_7[13:11]), .INPR(in_5[12]), .C(1'b0), .in_8(alu_12_out_10),
    .out_9(out_9[12]), .out_10(alu_13_out_10));
  ALU alu_14 (
    .in_1(T), .D(D), .IR(IR), .I(I), .DR(in_7[14:12]), .INPR(in_5[13]), .C(1'b0), .in_8(alu_13_out_10),
    .out_9(out_9[13]), .out_10(alu_14_out_10));
  ALU alu_15 (
    .in_1(T), .D(D), .IR(IR), .I(I), .DR(in_7[15:13]), .INPR(in_5[14]), .C(1'b0), .in_8(alu_14_out_10),
    .out_9(out_9[14]), .out_10(alu_15_out_10));
  ALU alu_16 (
    .in_1(T), .D(D), .IR(IR), .I(I), .DR({E, in_7[15:14]}), .INPR(in_5[15]), .C(1'b0), .in_8(alu_15_out_10),
    .out_9(out_9[15]), .out_10(alu_16_out_10));
  and and_4 (and_4_out, in_7[15], and_2_out);
  and and_5 (and_5_out, and_3_out, in_7[0]);
  or or_1 (E_2, alu_16_out_10, and_4_out, and_5_out);

  // Notes on the sheet:
  //   AC
  //   DR
endmodule

module AC_Controller (
  input  [15:0] in_1,
  input  [7:0] D,
  input  [15:0] in_3,
  input  I,
  output load,
  output inc,
  output clr
);

  wire and_1_out, and_2_out, and_3_out, and_4_out, and_5_out, and_6_out, and_7_out, and_8_out, not_1_out;

  not not_1 (not_1_out, I);
  and and_1 (and_1_out, D[7], in_1[3]);
  and and_2 (and_2_out, in_1[5], D[0]);
  and and_3 (and_3_out, in_1[5], D[1]);
  and and_4 (and_4_out, D[2], in_1[5]);
  and and_5 (and_5_out, and_1_out, not_1_out, in_3[6]);
  and and_6 (and_6_out, and_1_out, not_1_out, in_3[7]);
  and and_7 (and_7_out, and_1_out, not_1_out, in_3[9]);
  and and_8 (and_8_out, and_1_out, I, in_3[11]);
  and and_9 (inc, and_1_out, not_1_out, in_3[5]);
  and and_10 (clr, and_1_out, not_1_out, in_3[11]);
  or or_1 (load, and_2_out, and_3_out, and_4_out, and_5_out, and_6_out, and_7_out, and_8_out);

  // Notes on the sheet:
  //   T
  //   IR
endmodule

module E_Controller (
  input  [15:0] in_1,
  input  [7:0] D,
  input  [15:0] IR,
  input  I,
  input  E,
  input  ALU,
  output out_7
);

  wire and_1_out, and_2_out, and_3_out, and_4_out, and_5_out, and_6_out, and_7_out, and_8_out, not_1_out,
       not_2_out, or_1_out, or_2_out, or_3_out, xor_1_out;

  not not_1 (not_1_out, I);
  and and_1 (and_1_out, in_1[3], D[7], not_1_out);
  or or_1 (or_1_out, IR[6], IR[7]);
  and and_2 (and_2_out, in_1[5], D[1]);
  or or_2 (or_2_out, and_2_out, and_3_out);
  and and_3 (and_3_out, and_1_out, or_1_out);
  and and_4 (and_4_out, and_1_out, IR[10]);
  and and_5 (and_5_out, and_1_out, IR[8]);
  and and_6 (and_6_out, or_2_out, ALU);
  or or_3 (or_3_out, or_2_out, and_4_out, and_5_out);
  not not_2 (not_2_out, or_3_out);
  xor xor_1 (xor_1_out, and_5_out, E);
  and and_7 (and_7_out, xor_1_out, and_5_out);
  and and_8 (and_8_out, E, not_2_out);
  or or_4 (out_7, and_6_out, and_8_out, and_7_out);

  // Notes on the sheet:
  //   T
endmodule

module IR_Controller (
  input  [15:0] in_1,
  input  R,
  output out_3,
  output out_4,
  output out_5
);

  wire not_1_out;

  not not_1 (not_1_out, R);
  and and_1 (out_3, in_1[1], not_1_out);

  assign out_4 = 1'b0;
  assign out_5 = 1'b0;

  // Notes on the sheet:
  //   T
endmodule

module TR_Controller (
  input  [15:0] in_1,
  input  R,
  output out_3,
  output out_4,
  output out_5
);

  and and_1 (out_3, in_1[0], R);

  assign out_4 = 1'b0;
  assign out_5 = 1'b0;

  // Notes on the sheet:
  //   T
endmodule

module OUTR_Controller (
  input  [15:0] in_1,
  input  [7:0] D,
  input  [15:0] in_3,
  input  I,
  output out_5,
  output out_6,
  output out_7
);

  and and_1 (out_5, in_1[3], D[7], in_3[10], I);

  assign out_6 = 1'b0;
  assign out_7 = 1'b0;

  // Notes on the sheet:
  //   T
  //   IR
endmodule

module BUS_Controller (
  input  [15:0] T,
  input  [7:0] D,
  input  [15:0] in_3,
  input  I,
  input  R,
  output [2:0] out_6
);

  wire and_1_out, and_2_out, and_3_out, and_4_out, and_5_out, and_6_out, and_7_out, and_8_out, and_9_out,
       and_10_out, and_11_out, and_12_out, and_13_out, and_14_out, and_15_out, and_16_out, not_1_out,
       not_2_out, or_1_out, or_2_out, or_3_out, or_4_out;

  not not_1 (not_1_out, R);
  not not_2 (not_2_out, D[7]);
  and and_1 (and_1_out, T[4], D[4]);
  or or_1 (or_1_out, and_1_out, and_2_out);
  and and_2 (and_2_out, T[5], D[5]);
  and and_3 (and_3_out, T[0], not_1_out);
  or or_2 (or_2_out, and_3_out, and_4_out, and_5_out);
  and and_4 (and_4_out, T[0], R);
  and and_5 (and_5_out, T[4], D[5]);
  and and_6 (and_6_out, T[6], D[6]);
  and and_7 (and_7_out, T[4], D[3]);
  or or_3 (or_3_out, and_7_out, and_8_out);
  and and_8 (and_8_out, D[7], I, T[3], in_3[10]);
  and and_9 (and_9_out, T[2], not_1_out);
  and and_10 (and_10_out, T[1], R);
  and and_11 (and_11_out, T[1], not_1_out);
  and and_12 (and_12_out, not_2_out, T[3]);
  and and_13 (and_13_out, T[4], D[0]);
  and and_14 (and_14_out, T[4], D[1]);
  and and_15 (and_15_out, T[4], D[6]);
  and and_16 (and_16_out, D[2], T[4]);
  or or_4 (or_4_out, and_11_out, and_12_out, and_13_out, and_14_out, and_15_out, and_16_out);
  Priority_Encoder priority_encoder_1 (
    .in0(1'b1), .in1(or_1_out), .in2(or_2_out), .in3(and_6_out), .in4(or_3_out), .in5(and_9_out),
    .in6(and_10_out), .in7(or_4_out), .out(out_6), .en_in(1'b1));  // open: gs, en_out

  // Notes on the sheet:
  //   IR
endmodule

module SC_Controller (
  input  [15:0] T,
  input  [7:0] D,
  input  I,
  input  R,
  output out_5
);

  wire and_1_out, and_2_out, and_3_out, and_4_out, and_5_out, and_6_out, and_7_out, and_8_out, and_9_out,
       and_10_out, not_1_out;

  not not_1 (not_1_out, I);
  // NOT_Gate not_2 has open pins: in=R, out=open
  and and_1 (and_1_out, T[2], R);
  and and_2 (and_2_out, T[5], D[0]);
  and and_3 (and_3_out, T[5], D[1]);
  and and_4 (and_4_out, T[5], D[2]);
  and and_5 (and_5_out, T[4], D[3]);
  and and_6 (and_6_out, T[4], D[4]);
  and and_7 (and_7_out, T[5], D[5]);
  and and_8 (and_8_out, T[6], D[6]);
  and and_9 (and_9_out, T[3], D[7], not_1_out);
  and and_10 (and_10_out, T[3], D[7], I);
  or or_1 (out_5, and_1_out, and_2_out, and_3_out, and_4_out, and_5_out, and_6_out, and_7_out, and_8_out, and_9_out, and_10_out);
endmodule

module S_Controller (
  input  [15:0] in_1,
  input  [7:0] D,
  input  [15:0] in_3,
  input  I,
  output out_5
);

  wire not_1_out;

  not not_1 (not_1_out, I);
  and and_1 (out_5, in_1[3], D[7], in_3[0], not_1_out);

  // Notes on the sheet:
  //   T
  //   IR
endmodule
